# Fritzing sketch cnc_socketplate (saved by Fritzing 0.9.1b)
circuit board: 8.46667cm x 5.64444cm
breadboards: 1

parts:
  J1 = female pin header, 4 pins [form="♀ (female)"]
  J2 = female pin header, 4 pins [form="♀ (female)"]
  J3 = female pin header, 4 pins [form="♀ (female)"]
  J4 = female pin header, 4 pins [form="♀ (female)"]
  J5 = female pin header, 4 pins [form="♀ (female)"]
  J6 = female pin header, 4 pins [form="♀ (female)"]
  J7 = female pin header, 4 pins [form="♀ (female)"]
  J8 = female pin header, 4 pins [form="♀ (female)"]
  J9 = female pin header, 4 pins [form="♀ (female)"]
  J10 = female pin header, 4 pins [form="♀ (female)"]
  J11 = female pin header, 6 pins [form="♀ (female)"]
  J12 = female pin header, 6 pins [form="♀ (female)"]
  J13 = double row female pin header, 6 pins [form="♀ (female)"]
  J14 = double row female pin header, 6 pins [form="♀ (female)"]
  J15 = double row female pin header, 6 pins [form="♀ (female)"]
  J16 = double row female pin header, 4 pins [form="♀ (female)"]
  Pad1 = Pad [width=3 height=3 connect=center]
  Pad2 = Pad [width=3 height=3 connect=center]
  Pad3 = Pad [width=3 height=3 connect=center]
  Pad4 = Pad [width=3 height=3 connect=center]
  J17 = female pin header, 2 pins [form="♀ (female)"]
  J18 = female pin header, 2 pins [form="♀ (female)"]
  Pad5 = Pad [width=3 height=3 connect=center]
  Pad7 = Pad [width=3 height=3 connect=center]  # not connected
  Pad8 = Pad [width=3 height=3 connect=center]  # not connected
  Pad9 = Pad [width=3 height=3 connect=center]

nets:
  N1: J1.pin1, J2.pin1
  N2: J1.pin2, J2.pin2
  N3: J1.pin3, J2.pin3
  N4: J1.pin4, J2.pin4
  N5: J3.pin1, J4.pin1
  N6: J3.pin2, J4.pin2
  N7: J3.pin3, J4.pin3
  N8: J3.pin4, J4.pin4
  N9: J5.pin1, J6.pin1
  N10: J5.pin2, J6.pin2
  N11: J5.pin3, J6.pin3
  N12: J5.pin4, J6.pin4
  N13: J7.pin1, J8.pin1
  N14: J7.pin2, J8.pin2
  N15: J7.pin3, J8.pin3
  N16: J7.pin4, J8.pin4
  N17: J9.pin1, J10.pin1
  N18: J9.pin2, J10.pin2
  N19: J9.pin3, J10.pin3
  N20: J9.pin4, J10.pin4
  N21: J11.pin1, J11.pin2, J13.pin6, Pad9.pad
  N22: J11.pin3, J11.pin4, J13.pin5
  N23: J11.pin5, J11.pin6, J13.pin4
  N24: J12.pin1, J12.pin2, J13.pin1
  N25: J12.pin3, J12.pin4, J13.pin2
  N26: J12.pin5, J12.pin6, J13.pin3
  N27: J14.pin1, J15.pin6, J16.pin1
  N28: J14.pin2, J15.pin5, J16.pin2
  N29: J14.pin5, J15.pin2, Pad4.pad
  N30: J14.pin6, J15.pin1, Pad3.pad
  N31: J16.pin3, Pad2.pad
  N32: J16.pin4, Pad1.pad
  N33: J17.pin1, J18.pin1, Pad5.pad
  N34: J17.pin2, J18.pin2
