# Fritzing sketch cnc_socketplateV1.1 (saved by Fritzing 0.9.1b)
circuit board: 7.0195cm x 4.50155cm
breadboards: 1

parts:
  J1 = female pin header, 4 pins [form="♀ (female)"]
  J2 = female pin header, 4 pins [form="♀ (female)"]
  J3 = female pin header, 4 pins [form="♀ (female)"]
  J4 = female pin header, 4 pins [form="♀ (female)"]
  J5 = female pin header, 4 pins [form="♀ (female)"]
  J6 = female pin header, 4 pins [form="♀ (female)"]
  J7 = female pin header, 4 pins [form="♀ (female)"]
  J8 = female pin header, 4 pins [form="♀ (female)"]
  J9 = female pin header, 4 pins [form="♀ (female)"]
  J10 = female pin header, 4 pins [form="♀ (female)"]
  J11 = female pin header, 6 pins [form="♀ (female)"]
  J12 = female pin header, 6 pins [form="♀ (female)"]
  J14 = double row female pin header, 6 pins [form="♀ (female)"]
  J15 = double row female pin header, 6 pins [form="♀ (female)"]
  J18 = female pin header, 2 pins [form="♀ (female)"]
  Pad7 = Pad [width=3 height=3 connect=center]  # not connected
  Pad8 = Pad [width=3 height=3 connect=center]  # not connected
  J20 = female pin header, 4 pins [form="♀ (female)"]
  J19 = female pin header, 5 pins [form="♀ (female)"]
  Pad12 = Pad [width=3 height=3 connect=center]  # not connected
  Pad13 = Pad [width=3 height=3 connect=center]  # not connected
  Pad14 = Pad [width=3 height=3 connect=center]  # not connected
  Pad15 = Pad [width=3 height=3 connect=center]  # not connected
  Pad16 = Pad [width=3 height=3 connect=center]
  Pad17 = Pad [width=3 height=3 connect=center]  # not connected
  Pad18 = Pad [width=3 height=3 connect=center]  # not connected

nets:
  N1: J1.pin1, J2.pin1
  N2: J1.pin2, J2.pin2
  N3: J1.pin3, J2.pin3
  N4: J1.pin4, J2.pin4
  N5: J3.pin1, J4.pin1
  N6: J3.pin2, J4.pin2
  N7: J3.pin3, J4.pin3
  N8: J3.pin4, J4.pin4
  N9: J5.pin1, J6.pin1
  N10: J5.pin2, J6.pin2
  N11: J5.pin3, J6.pin3
  N12: J5.pin4, J6.pin4
  N13: J7.pin1, J8.pin1
  N14: J7.pin2, J8.pin2
  N15: J7.pin3, J8.pin3
  N16: J7.pin4, J8.pin4
  N17: J9.pin1, J10.pin1
  N18: J9.pin2, J10.pin2
  N19: J9.pin3, J10.pin3
  N20: J9.pin4, J10.pin4
  N21: J11.pin1, J11.pin2, J11.pin3, J11.pin4, J11.pin5, J11.pin6, J14.pin1, J15.pin1, J18.pin1, J19.pin2
  N22: J12.pin1, J12.pin2, J20.pin1
  N23: J12.pin3, J12.pin4, J20.pin2
  N24: J12.pin5, J12.pin6, J20.pin3
  N25: J14.pin2, J15.pin2, J19.pin4
  N26: J14.pin5, J15.pin5
  N27: J14.pin6, J15.pin6, J19.pin3
  N28: J18.pin2, J20.pin4
  N29: J19.pin5, Pad16.pad
