# Fritzing sketch limitswitchbuffer (saved by Fritzing 0.9.1b)
circuit board: 3.73197cm x 3.70819cm
breadboards: 1

parts:
  J1 = female pin header, 6 pins [form="♀ (female)"]
  R1 = Resistor [tolerance=±5% resistance=220 package=THT]
  U1 = TLP621 [package=THT]
  U2 = TLP621 [package=THT]
  U3 = TLP621 [package=THT]
  R2 = Resistor [tolerance=±5% resistance=220 package=THT]
  R3 = Resistor [tolerance=±5% resistance=220 package=THT]
  R4 = Resistor [tolerance=±5% resistance=220 package=THT]
  R5 = Resistor [tolerance=±5% resistance=220 package=THT]
  R6 = Resistor [tolerance=±5% resistance=220 package=THT]
  J2 = female pin header, 6 pins [form="♀ (female)"]

nets:
  N1: J1.pin1, U1.Pin_3, U2.Pin_3, U3.Pin_3, J2.pin1
  N2: J1.pin2, R1.Pin_1, R2.Pin_1, R3.Pin_1, R4.Pin_0, R5.Pin_1, R6.Pin_0, J2.pin2
  N3: J1.pin3, U1.Pin_2
  N4: J1.pin4, U2.Pin_2
  N5: J1.pin5, U3.Pin_2
  N6: J1.pin6, J2.pin6
  N7: R1.Pin_0, U1.Pin_1
  N8: U1.Pin_4, R4.Pin_1, J2.pin3
  N9: U2.Pin_1, R2.Pin_0
  N10: U2.Pin_4, R5.Pin_0, J2.pin4
  N11: U3.Pin_1, R3.Pin_0
  N12: U3.Pin_4, R6.Pin_1, J2.pin5
